// Logisim project Somador4bits.circ as structural Verilog: 4 circuits, main circuit main
// MS
module main (
  input  [3:0] in_1,
  input  [3:0] in_2
);

  wire [3:0] somador4b_1_out_3;

  Somador4B somador4b_1 (.out_3(somador4b_1_out_3), .in_1(in_1), .in_2(in_2));
  Hex_Digit_Display hex_digit_display_1 (.value(somador4b_1_out_3));  // open: dp
endmodule

module MS (
  input  A,
  input  B,
  output S,
  output Ts
);

  xor xor_1 (S, A, B);
  and and_1 (Ts, A, B);
endmodule

module SC (
  input  A,
  input  B,
  input  Te,
  output S,
  output Ts
);

  wire and_1_out, and_2_out, and_3_out, xor_1_out;

  xor xor_1 (xor_1_out, A, B);
  and and_1 (and_1_out, A, B);
  and and_2 (and_2_out, A, Te);
  and and_3 (and_3_out, B, Te);
  xor xor_2 (S, xor_1_out, Te);
  or or_1 (Ts, and_1_out, and_2_out, and_3_out);
endmodule

// SB
module Somador4B (
  input  [3:0] in_1,
  input  [3:0] in_2,
  output [3:0] out_3
);

  wire ms_1_ts, sc_2_ts, sc_3_ts;

  SC sc_1 (.S(out_3[3]), .A(in_1[3]), .B(in_2[3]), .Te(sc_2_ts));  // open: Ts
  SC sc_2 (.S(out_3[2]), .Ts(sc_2_ts), .A(in_1[2]), .B(in_2[2]), .Te(sc_3_ts));
  SC sc_3 (.S(out_3[1]), .Ts(sc_3_ts), .A(in_1[1]), .B(in_2[1]), .Te(ms_1_ts));
  MS ms_1 (.A(in_1[0]), .B(in_2[0]), .S(out_3[0]), .Ts(ms_1_ts));
endmodule
