// Logisim project SomadorSubtrator.circ as structural Verilog: 5 circuits, main circuit main
module main (
  input  in_1
);

  wire _0_2_out, _0_out, _1_2_out, _1_out, _2_2_out, _2_out, _3_2_out, _3_out, _4_2_out, _4_out, _5_2_out,
       _5_out, _6_2_out, _6_out, _7_2_out, _7_out, _8_2_out, _8_out, _9_2_out, _9_out, decod7s_1_a,
       decod7s_1_b, decod7s_1_c, decod7s_1_d, decod7s_1_e, decod7s_1_f, decod7s_1_g;
  wire [3:0] ss4bits_1_out_4, teclado_1_out_11, teclado_2_out_11;

  Button _1 (.out(_1_out));
  Button _0 (.out(_0_out));
  Button _2 (.out(_2_out));
  Teclado teclado_1 (
    .out_11(teclado_1_out_11), .in_1(_0_out), .in_2(_1_out), .in_3(_2_out), .in_4(_3_out), .in_5(_4_out),
    .in_6(_5_out), .in_7(_6_out), .in_8(_7_out), .in_9(_8_out), .in_10(_9_out));
  Button _5 (.out(_5_out));
  Button _4 (.out(_4_out));
  Button _6 (.out(_6_out));
  Button _3 (.out(_3_out));
  Button _9 (.out(_9_out));
  Button _7 (.out(_7_out));
  Button _8 (.out(_8_out));
  Hex_Digit_Display hex_digit_display_1 (.value(teclado_1_out_11));  // open: dp
  Button _2_2 (.out(_2_2_out));
  Button _0_2 (.out(_0_2_out));
  Button _1_2 (.out(_1_2_out));
  Teclado teclado_2 (
    .out_11(teclado_2_out_11), .in_1(_0_2_out), .in_2(_1_2_out), .in_3(_2_2_out), .in_4(_3_2_out),
    .in_5(_4_2_out), .in_6(_5_2_out), .in_7(_6_2_out), .in_8(_7_2_out), .in_9(_8_2_out), .in_10(_9_2_out));
  SS4bits ss4bits_1 (.in_1(teclado_1_out_11), .in_3(in_1), .in_2(teclado_2_out_11), .out_4(ss4bits_1_out_4));
  Button _3_2 (.out(_3_2_out));
  Button _5_2 (.out(_5_2_out));
  Button _4_2 (.out(_4_2_out));
  Button _6_2 (.out(_6_2_out));
  Hex_Digit_Display hex_digit_display_2 (.value(teclado_2_out_11));  // open: dp
  Decod7s decod7s_1 (
    .in_1(ss4bits_1_out_4), .a(decod7s_1_a), .b(decod7s_1_b), .c(decod7s_1_c), .d(decod7s_1_d),
    .e(decod7s_1_e), .f(decod7s_1_f), .g(decod7s_1_g));
  Button _7_2 (.out(_7_2_out));
  Button _8_2 (.out(_8_2_out));
  Button _9_2 (.out(_9_2_out));
  _7_Segment_Display u_7_segment_display_1 (
    .g(decod7s_1_g), .f(decod7s_1_f), .a(decod7s_1_a), .b(decod7s_1_b), .e(decod7s_1_e), .d(decod7s_1_d),
    .c(decod7s_1_c));  // open: dp
endmodule

module SSC (
  input  O,
  input  A,
  input  B,
  input  Te,
  output S,
  output TS
);

  wire and_1_out, and_2_out, or_1_out, xor_1_out, xor_2_out;

  xor xor_1 (xor_1_out, A, B);
  and and_1 (and_1_out, B, Te);
  xor xor_2 (xor_2_out, O, A);
  or or_1 (or_1_out, Te, B);
  and and_2 (and_2_out, xor_2_out, or_1_out);
  xor xor_3 (S, xor_1_out, Te);
  or or_2 (TS, and_1_out, and_2_out);
endmodule

module MMS (
  input  O,
  input  A,
  input  B,
  output S,
  output Ts
);

  wire xor_2_out;

  xor xor_1 (S, A, B);
  xor xor_2 (xor_2_out, O, A);
  and and_1 (Ts, xor_2_out, B);
endmodule

// SS4B
module SS4bits (
  input  [3:0] in_1,
  input  [3:0] in_2,
  input  in_3,
  output [3:0] out_4
);

  wire mms_1_ts, ssc_2_ts, ssc_3_ts;

  SSC ssc_1 (.O(in_3), .A(in_1[3]), .B(in_2[3]), .Te(ssc_2_ts), .S(out_4[3]));  // open: TS
  SSC ssc_2 (.O(in_3), .A(in_1[2]), .B(in_2[2]), .Te(ssc_3_ts), .S(out_4[2]), .TS(ssc_2_ts));
  SSC ssc_3 (.O(in_3), .A(in_1[1]), .B(in_2[1]), .Te(mms_1_ts), .S(out_4[1]), .TS(ssc_3_ts));
  MMS mms_1 (.S(out_4[0]), .Ts(mms_1_ts), .O(in_3), .A(in_1[0]), .B(in_2[0]));
endmodule

module TESTE (
  input  [3:0] in_1,
  input  [3:0] in_2,
  input  in_3
);

  wire [3:0] ss4bits_1_out_4;

  SS4bits ss4bits_1 (.in_1(in_1), .in_3(in_3), .in_2(in_2), .out_4(ss4bits_1_out_4));
  Hex_Digit_Display hex_digit_display_1 (.value(ss4bits_1_out_4));  // open: dp
endmodule
