// Logisim project Teclado.circ as structural Verilog: 2 circuits, main circuit Codificador
module Codificador (
  input  T0,
  input  T1,
  input  T2,
  input  T3,
  input  T4,
  input  T5,
  input  T6,
  input  T7,
  input  T8,
  input  T9,
  output [3:0] out_11
);

  or or_1 (out_11[3], T9, T8);
  or or_2 (out_11[2], T7, T6, T5, T4);
  or or_3 (out_11[1], T7, T6, T3, T2);
  or or_4 (out_11[0], T9, T7, T5, T3, T1);
endmodule

module Teclado (
  input  in_1,
  input  in_2,
  input  in_3,
  input  in_4,
  input  in_5,
  input  in_6,
  input  in_7,
  input  in_8,
  input  in_9,
  input  in_10,
  output [3:0] out_11
);

  wire or_1_out;
  wire [3:0] codificador_1_out_11;

  Codificador codificador_1 (
    .out_11(codificador_1_out_11), .T0(in_1), .T1(in_2), .T2(in_3), .T3(in_4), .T4(in_5), .T5(in_6),
    .T6(in_7), .T7(in_8), .T8(in_9), .T9(in_10));
  or or_1 (or_1_out, in_1, in_2, in_3, in_4, in_5, in_6, in_7, in_8, in_9, in_10);
  Register #(.width(4), .trigger("falling"), .Select("low")) register_1 (
    .D(codificador_1_out_11), .Q(out_11), .clk(or_1_out));  // open: en, clr
endmodule
