// Logisim project enviar_discord_3.circ as structural Verilog: 4 circuits, main circuit main
module main (
  input  [3:0] in_1,
  input  [3:0] in_2,
  input  in_3,
  output [3:0] out_4
);

  wire primeiro_2_out_5, primeiro_3_out_5, primeiro_4_out_5;

  primeiro primeiro_1 (.out_6(out_4[3]), .O(in_3), .A(in_1[3]), .B(in_2[3]), .TE(primeiro_2_out_5));  // open: out_5
  primeiro primeiro_2 (
    .out_5(primeiro_2_out_5), .out_6(out_4[2]), .O(in_3), .A(in_1[2]), .B(in_2[2]), .TE(primeiro_3_out_5));
  primeiro primeiro_3 (
    .out_5(primeiro_3_out_5), .out_6(out_4[1]), .O(in_3), .A(in_1[1]), .B(in_2[1]), .TE(primeiro_4_out_5));
  primeiro primeiro_4 (.out_5(primeiro_4_out_5), .out_6(out_4[0]), .O(in_3), .A(in_1[0]), .B(in_2[0]), .TE(1'b0));
endmodule

// SSC
module primeiro (
  input  O,
  input  A,
  input  B,
  input  TE,
  output out_5,
  output out_6
);

  wire and_1_out, and_2_out, or_1_out, xor_1_out, xor_2_out;

  xor xor_1 (xor_1_out, A, B);
  and and_1 (and_1_out, B, TE);
  xor xor_2 (xor_2_out, O, A);
  or or_1 (or_1_out, TE, B);
  xor xor_3 (out_5, xor_1_out, TE);
  and and_2 (and_2_out, xor_2_out, or_1_out);
  or or_2 (out_6, and_1_out, and_2_out);
endmodule

// SS4B
module Calculadora_mais_E_menos (
  input  [3:0] in_1,
  input  [3:0] in_2,
  input  in_3,
  output [3:0] out_4
);

  wire primeiro_2_out_5, primeiro_3_out_5, primeiro_4_out_5;

  primeiro primeiro_1 (.out_6(out_4[3]), .O(in_3), .A(in_1[3]), .B(in_2[3]), .TE(primeiro_2_out_5));  // open: out_5
  primeiro primeiro_2 (
    .out_5(primeiro_2_out_5), .out_6(out_4[2]), .O(in_3), .A(in_1[2]), .B(in_2[2]), .TE(primeiro_3_out_5));
  primeiro primeiro_3 (
    .out_5(primeiro_3_out_5), .out_6(out_4[1]), .O(in_3), .A(in_1[1]), .B(in_2[1]), .TE(primeiro_4_out_5));
  primeiro primeiro_4 (.out_5(primeiro_4_out_5), .out_6(out_4[0]), .O(in_3), .A(in_1[0]), .B(in_2[0]), .TE(1'b0));
endmodule

module brincando (
  input  [3:0] in_1,
  input  [3:0] in_2,
  input  in_3
);

  wire [3:0] calculadora_mais_e_menos_1_out_4;

  Calculadora_mais_E_menos calculadora_mais_e_menos_1 (
    .in_1(in_1), .in_3(in_3), .in_2(in_2), .out_4(calculadora_mais_e_menos_1_out_4));
  Hex_Digit_Display hex_digit_display_1 (.value(calculadora_mais_e_menos_1_out_4));  // open: dp
endmodule
