// Logisim project enviar_marcos_trab.circ as structural Verilog: 6 circuits, main circuit main
module main (
  input  [3:0] in_1,
  input  [3:0] in_2,
  input  in_3,
  output [3:0] out_4
);

  wire mms_1_s, ssc_2_out_6, ssc_3_out_6;

  SSC ssc_1 (.out_5(out_4[3]), .O(in_3), .A(in_1[3]), .B(in_2[3]), .TE(ssc_2_out_6));  // open: out_6
  SSC ssc_2 (.out_5(out_4[2]), .out_6(ssc_2_out_6), .O(in_3), .A(in_1[2]), .B(in_2[2]), .TE(ssc_3_out_6));
  SSC ssc_3 (.out_5(out_4[1]), .out_6(ssc_3_out_6), .O(in_3), .A(in_1[1]), .B(in_2[1]), .TE(mms_1_s));
  MMS mms_1 (.S(mms_1_s), .TS(out_4[0]), .O(in_3), .A(in_1[0]), .B(in_2[0]));
endmodule

module SSC (
  input  O,
  input  A,
  input  B,
  input  TE,
  output out_5,
  output out_6
);

  wire and_1_out, and_2_out, or_1_out, xor_1_out, xor_2_out;

  xor xor_1 (xor_1_out, A, B);
  and and_1 (and_1_out, B, TE);
  xor xor_2 (xor_2_out, O, A);
  or or_1 (or_1_out, TE, B);
  xor xor_3 (out_5, xor_1_out, TE);
  and and_2 (and_2_out, xor_2_out, or_1_out);
  or or_2 (out_6, and_1_out, and_2_out);
endmodule

module SS4B (
  input  [3:0] in_1,
  input  [3:0] in_2,
  input  in_3,
  output [3:0] out_4
);

  wire ssc_2_out_6, ssc_3_out_6, ssc_4_out_6;

  SSC ssc_1 (.out_5(out_4[3]), .O(in_3), .A(in_1[3]), .B(in_2[3]), .TE(ssc_2_out_6));  // open: out_6
  SSC ssc_2 (.out_5(out_4[2]), .out_6(ssc_2_out_6), .O(in_3), .A(in_1[2]), .B(in_2[2]), .TE(ssc_3_out_6));
  SSC ssc_3 (.out_5(out_4[1]), .out_6(ssc_3_out_6), .O(in_3), .A(in_1[1]), .B(in_2[1]), .TE(ssc_4_out_6));
  SSC ssc_4 (.out_5(out_4[0]), .out_6(ssc_4_out_6), .O(in_3), .A(in_1[0]), .B(in_2[0]), .TE(1'b0));
endmodule

module MMS (
  input  O,
  input  A,
  input  B,
  output S,
  output TS
);

  wire and_1_out, and_2_out, not_1_out, not_2_out;

  not not_1 (not_1_out, O);
  not not_2 (not_2_out, A);
  and and_1 (and_1_out, not_1_out, B, A);
  and and_2 (and_2_out, O, not_2_out, B);
  xor xor_1 (S, A, B);
  or or_1 (TS, and_1_out, and_2_out);
endmodule

module MSS_MAIN (
  input  [3:0] in_1,
  input  [3:0] in_2,
  input  in_3,
  output [3:0] out_4
);

  wire mms_1_s, ssc_2_out_6, ssc_3_out_6;

  SSC ssc_1 (.out_5(out_4[3]), .O(in_3), .A(in_1[3]), .B(in_2[3]), .TE(ssc_2_out_6));  // open: out_6
  SSC ssc_2 (.out_5(out_4[2]), .out_6(ssc_2_out_6), .O(in_3), .A(in_1[2]), .B(in_2[2]), .TE(ssc_3_out_6));
  SSC ssc_3 (.out_5(out_4[1]), .out_6(ssc_3_out_6), .O(in_3), .A(in_1[1]), .B(in_2[1]), .TE(mms_1_s));
  MMS mms_1 (.S(mms_1_s), .TS(out_4[0]), .O(in_3), .A(in_1[0]), .B(in_2[0]));
endmodule

module MSS_TESTE (
  input  [3:0] in_1,
  input  [3:0] in_2,
  input  in_3
);

  wire [3:0] mss_main_1_out_4;

  MSS_MAIN mss_main_1 (.in_1(in_1), .in_3(in_3), .in_2(in_2), .out_4(mss_main_1_out_4));
  Hex_Digit_Display hex_digit_display_1 (.value(mss_main_1_out_4));  // open: dp
endmodule
